# Fritzing sketch Schematic ESP32 Version (saved by Fritzing 0.9.6b)

parts:
  HC-SR04_Sensor_1 = HC-SR04 Ultrasonic Distance Sensor
  U1 = ESP32-38PinWide [part_number=ESP32-38PinWide]
  S1 = Pololu QTR-8 Reflectabce Sensor array [package=THT]
  M1 = DC Motor
  M2 = DC Motor
  LLC1 = Logic Level Converter [package="Breakout board"]
  U2 = LIPO-110mAh [package=lipo-110]
  U3 = LIPO-110mAh [package=lipo-110]
  U4 = LIPO-110mAh [package=lipo-110]
  U5 = SWITCH_SPDT [package=kps-1290]
  S2 = Pololu DRV 8833 Dual Motor Driver Carrier [part_number=DRV8833]
  S2_1 = Pololu DRV 8833 Dual Motor Driver Carrier [part_number=DRV8833]  # not connected
  S2_2 = Pololu DRV 8833 Dual Motor Driver Carrier [part_number=DRV8833]  # not connected

nets:
  N1: HC-SR04_Sensor_1.VCC, U1.3.3, S1.pin2, S1.pin14
  N2: HC-SR04_Sensor_1.TRIG, U1.GPIO33
  N3: HC-SR04_Sensor_1.ECHO, U1.GPIO32
  N4: HC-SR04_Sensor_1.GND, U1.GPIO11
  GND: U1.GND, S1.pin1, S1.pin15, LLC1.L-GND, LLC1.H-GND, U4.-, S2.connector1, S2.GND
  VIN: U1.VIN, LLC1.HV, S2.VIN
  N5: U1.GPIO15, S1.pin12
  N6: U1.GPIO2, S1.pin11
  N7: U1.GPIO0, S1.pin10
  N8: U1.GPIO4, S1.pin9
  N9: U1.GPIO16, S1.pin8
  N10: U1.GPIO17, LLC1.LV4
  N11: U1.GPIO5, LLC1.LV3
  N12: U1.GPIO18, LLC1.LV2
  N13: U1.GPIO19, LLC1.LV1
  N14: S1.pin24, S1.pin25
  N15: M1.pin_1, S2.AOUT2
  N16: M1.pin_2, S2.AOUT1
  N17: M2.pin_1, S2.BOUT1
  N18: M2.pin_2, S2.BOUT2
  N19: LLC1.HV4, S2.connector6
  N20: LLC1.HV3, S2.connector5
  N21: LLC1.HV2, S2.connector4
  N22: LLC1.HV1, S2.connector3
  N23: U2.+, U5.O
  N24: U2.-, U3.+
  N25: U3.-, U4.+
  N26: U5.S, S2.connector2

custom parts:
  ESP32-38PinWide: Generic 38-Pin ESP32 with wide format (only access to one side of pins on a breadboard) based on Stephen Lilley's HiLetgo ESP-WROOM-32 ESP32 ESP-32S Development Board.
  Logic Level Converter: 5V to/from 3.3V logic level converter
